# Fritzing sketch ProjectorSweep (saved by Fritzing 0.7.11b)

parts:
  Arduino1 = Arduino
  SONAR1 = Maxbotix MaxSonar Ultrasonic Sensor
  J1 = Basic Servo

nets:
  GND: Arduino1.GND, SONAR1.BW, J1.gnd
  N1: Arduino1.D9, J1.pulse
  N2: Arduino1.3V3, SONAR1.PW
  +5V: Arduino1.+5V, J1.vcc
  N3: Arduino1.A0, SONAR1.TX

custom parts:
  Maxbotix MaxSonar Ultrasonic Sensor: Maxbotix MaxSonar Ultrasonic Sensor LV-EZ0, LV-EZ1, LV-EZ2, LV-EZ3, LV-EZ4
